# Fritzing sketch Sketch (saved by Fritzing 0.9.6b)
circuit board: 20.0624cm x 11.9913cm

parts:
  SM1 = 28BYJ-48 Stepper Motor [part_number=28BYJ-48]
  A2 = Fydun UNL2003 stepper driver
  VCC1 = Battery
  U1 = Voltage Regulator -- 3.3 V -- LM1117
  C1 = Electrolytic Capacitor [capacitance=10μF voltage=35V package="0605 [SMD, electrolytic]"]
  C2 = Electrolytic Capacitor [capacitance=10μF voltage=35V package="0605 [SMD, electrolytic]"]
  C3 = Ceramic Capacitor [capacitance=100nF voltage=35V package="100 mil [THT, multilayer]"]
  C4 = Ceramic Capacitor [capacitance=100nF voltage=35V package="100 mil [THT, multilayer]"]
  U2 = Voltage Regulator - 5V [package="TO220 [THT]"]
  C6 = Electrolytic Capacitor [capacitance=10μF voltage=35V package="0605 [SMD, electrolytic]"]
  C8 = Ceramic Capacitor [capacitance=100nF voltage=35V package="100 mil [THT, multilayer]"]
  C5 = Electrolytic Capacitor [capacitance=10μF voltage=35V package="0605 [SMD, electrolytic]"]
  C7 = Ceramic Capacitor [capacitance=100nF voltage=35V package="100 mil [THT, multilayer]"]
  IR1 = vs1838b [package=THT]
  A1 = MH-ET Live Minikit for ESP32

nets:
  N1: SM1.blue-pin, A2.Pin_15
  N2: SM1.pink-pin, A2.Pin_14
  N3: SM1.yellow-pin, A2.Pin_13
  N4: SM1.orange-pin, A2.Pin_12
  N5: SM1.red-pin, A2.Pin_9, A2.Pin_10, A2.Pin_11, A2.Pin_16, U2.output_voltage, C6.+, C8.1, IR1.Vs
  GND: A2.Pin_8, VCC1.-, U1.GND, C1.-, C2.-, C3.1, C4.0, U2.GND, C6.-, C8.0, C5.-, C7.1, IR1.GND, A1.GND
  N6: VCC1.+, U1.IN, C1.+, C3.0, U2.input_voltage, C5.+, C7.0
  N7: U1.OUT, C2.+, C4.1, A1.VCC
  N8: IR1.Data, A1.IO26, A1.IO27

notes:
  ~12v
  3.3v
  5v
  ESP32
  Driver & StepMotor

custom parts:
  28BYJ-48 Stepper Motor: Unipolar Stepper Motor 28BYJ-48 Top coil - pink & orange Bottom coil - blue & yellow Common rail - red Connector pins: blue - pink - yellow - orange - red
  Fydun UNL2003 stepper driver: Fydun UNL2003 stepper driver board.
  Battery: Your standard 3x 18650 battery pack (11.1 Volts)
  Voltage Regulator -- 3.3 V -- LM1117: LM1117-3.3 Voltage regulator, 3.3 V output. Note that the pinout order is not the same as LM7805 or LM7833.
  MH-ET Live Minikit for ESP32: MH-ET Live Minikit for ESP32 ( http://mh.nodebb.com/topic/8/mh-et-live-minikit-for-esp32/2/) PCB footprint is invalid.
